// Logisim project Practica4-Arquitectura.circ as structural Verilog: 4 circuits, main circuit Half adder
module Sumador (
  input  Numero_1,
  input  in_2,
  input  in_3,
  input  in_4,
  input  in_5,
  input  in_6,
  input  in_7,
  input  in_8,
  input  in_9,
  input  Numero_2,
  input  in_11,
  input  in_12,
  input  in_13,
  input  in_14,
  input  in_15,
  input  in_16,
  output Resultado,
  output out_18,
  output out_19,
  output out_20,
  output out_21,
  output out_22,
  output out_23,
  output out_24,
  output Desbordamiento
);

  wire full_adder_1_acarreo, full_adder_2_acarreo, full_adder_3_acarreo, full_adder_4_acarreo,
       full_adder_5_acarreo, full_adder_6_acarreo, half_adder_1_acarreo;

  Full_adder full_adder_1 (
    .X(in_7), .Carreo(half_adder_1_acarreo), .y(in_16), .Acarreo(full_adder_1_acarreo), .Suma(out_23));
  Half_adder half_adder_1 (.X(in_8), .Y(in_9), .Acarreo(half_adder_1_acarreo), .Suma(out_24));
  Full_adder full_adder_2 (
    .X(in_6), .Carreo(full_adder_1_acarreo), .y(in_15), .Acarreo(full_adder_2_acarreo), .Suma(out_22));
  Full_adder full_adder_3 (
    .X(in_5), .Carreo(full_adder_2_acarreo), .y(in_14), .Acarreo(full_adder_3_acarreo), .Suma(out_21));
  Full_adder full_adder_4 (
    .X(in_4), .Carreo(full_adder_3_acarreo), .y(in_13), .Acarreo(full_adder_4_acarreo), .Suma(out_20));
  Full_adder full_adder_5 (
    .X(in_3), .Carreo(full_adder_4_acarreo), .y(in_12), .Acarreo(full_adder_5_acarreo), .Suma(out_19));
  Full_adder full_adder_6 (
    .X(in_2), .Carreo(full_adder_5_acarreo), .y(in_11), .Acarreo(full_adder_6_acarreo), .Suma(out_18));
  Full_adder full_adder_7 (
    .X(Numero_1), .Carreo(full_adder_6_acarreo), .y(Numero_2), .Acarreo(Desbordamiento), .Suma(Resultado));

  // Notes on the sheet:
  //   +
endmodule

module Restador (
  input  Numero_1,
  input  in_2,
  input  in_3,
  input  in_4,
  input  in_5,
  input  in_6,
  input  in_7,
  input  in_8,
  input  in_9,
  input  Numero_2,
  input  in_11,
  input  in_12,
  input  in_13,
  input  in_14,
  input  in_15,
  input  in_16,
  output Resultado,
  output out_18,
  output out_19,
  output out_20,
  output out_21,
  output out_22,
  output out_23,
  output out_24,
  output Complemento_a_2
);

  wire full_adder_1_acarreo, full_adder_2_acarreo, full_adder_3_acarreo, full_adder_4_acarreo,
       full_adder_5_acarreo, full_adder_6_acarreo, full_adder_7_acarreo, full_adder_8_acarreo, not_1_out,
       not_2_out, not_3_out, not_4_out, not_5_out, not_6_out, not_7_out, not_8_out;

  not not_1 (not_1_out, in_9);
  not not_2 (not_2_out, in_16);
  not not_3 (not_3_out, in_15);
  not not_4 (not_4_out, in_14);
  not not_5 (not_5_out, in_13);
  not not_6 (not_6_out, in_12);
  not not_7 (not_7_out, in_11);
  not not_8 (not_8_out, Numero_2);
  not not_9 (Complemento_a_2, full_adder_8_acarreo);
  Full_adder full_adder_1 (
    .X(in_7), .Carreo(full_adder_2_acarreo), .y(not_2_out), .Acarreo(full_adder_1_acarreo), .Suma(out_23));
  Full_adder full_adder_2 (.X(1'b1), .Carreo(in_8), .y(not_1_out), .Acarreo(full_adder_2_acarreo), .Suma(out_24));
  Full_adder full_adder_3 (
    .X(in_6), .Carreo(full_adder_1_acarreo), .y(not_3_out), .Acarreo(full_adder_3_acarreo), .Suma(out_22));
  Full_adder full_adder_4 (
    .X(in_5), .Carreo(full_adder_3_acarreo), .y(not_4_out), .Acarreo(full_adder_4_acarreo), .Suma(out_21));
  Full_adder full_adder_5 (
    .X(in_4), .Carreo(full_adder_4_acarreo), .y(not_5_out), .Acarreo(full_adder_5_acarreo), .Suma(out_20));
  Full_adder full_adder_6 (
    .X(in_3), .Carreo(full_adder_5_acarreo), .y(not_6_out), .Acarreo(full_adder_6_acarreo), .Suma(out_19));
  Full_adder full_adder_7 (
    .X(in_2), .Carreo(full_adder_6_acarreo), .y(not_7_out), .Acarreo(full_adder_7_acarreo), .Suma(out_18));
  Full_adder full_adder_8 (
    .X(Numero_1), .Carreo(full_adder_7_acarreo), .y(not_8_out), .Acarreo(full_adder_8_acarreo),
    .Suma(Resultado));

  // Notes on the sheet:
  //   +
endmodule

module Full_adder (
  input  X,
  input  Carreo,
  input  y,
  output Acarreo,
  output Suma
);

  wire half_adder_1_acarreo, half_adder_1_suma, half_adder_2_acarreo;

  Half_adder half_adder_1 (.X(X), .Y(Carreo), .Acarreo(half_adder_1_acarreo), .Suma(half_adder_1_suma));
  Half_adder half_adder_2 (.X(half_adder_1_suma), .Y(y), .Acarreo(half_adder_2_acarreo), .Suma(Suma));
  or or_1 (Acarreo, half_adder_1_acarreo, half_adder_2_acarreo);
endmodule

module Half_adder (
  input  X,
  input  Y,
  output Acarreo,
  output Suma
);

  and and_1 (Acarreo, X, Y);
  xor xor_1 (Suma, X, Y);
endmodule
