// Logisim project Practica5.circ as structural Verilog
module Flip_Flop_SR (
  input  S,
  input  R,
  output Q,
  output Q_prime
);

  wire clock_1_out;

  Clock clock_1 (.out(clock_1_out));
  nor nor_1 (Q, S, clock_1_out, Q_prime);
  nor nor_2 (Q_prime, Q, clock_1_out, R);
endmodule

module _1__Automata (
  input  In,
  output out_2,
  output out_3,
  output out_4
);

  wire and_1_out, and_2_out, and_3_out, and_4_out, and_5_out, and_6_out, not_1_out, not_2_out, not_3_out,
       not_4_out, not_5_out, not_6_out, or_1_out;

  not not_1 (not_1_out, In);
  not not_2 (not_2_out, out_2);
  not not_3 (not_3_out, out_4);
  and and_1 (and_1_out, not_1_out, out_4, not_2_out);
  and and_2 (and_2_out, not_1_out, out_4, out_2);
  and and_3 (and_3_out, not_3_out, not_1_out);
  or or_1 (or_1_out, out_4, In);
  // Flip_Flop_SR flip_flop_sr_1: pin names not known; wires that end beside it: and_1_out, and_2_out, out_2
  // Flip_Flop_SR flip_flop_sr_2: pin names not known; wires that end beside it: and_3_out, or_1_out, out_4
  not not_4 (not_4_out, out_4);
  and and_4 (and_4_out, out_2, not_4_out);
  and and_5 (and_5_out, out_2, In);
  not not_5 (not_5_out, out_2);
  and and_6 (and_6_out, not_5_out, out_4, not_6_out);
  not not_6 (not_6_out, In);
  or or_2 (out_3, and_4_out, and_5_out, and_6_out);

  // Notes on the sheet:
  //   S0
  //   SL
  //   Out
endmodule
